# Fritzing sketch oled-wiring (saved by Fritzing 0.9.10b)

parts:
  Mod1 = Raspberry Pi 4B
  OLED_I2C1 = OLED 128x64 I2C Monochrome Display

nets:
  3V3: Mod1.3V3, OLED_I2C1.VDD
  N1: Mod1.GPIO2, OLED_I2C1.SDA
  N2: Mod1.GPIO3, OLED_I2C1.SCK
  GND: Mod1.GND, OLED_I2C1.GND
