# Fritzing sketch IoT Button V2 (saved by Fritzing 1.0.0rc)
breadboards: 1

parts:
  Mod1 = Raspberry Pi Pico W
  OLED_I2C1 = OLED 128x64 I2C Monochrome Display
  S1 = Round Pushbutton
  J1 = Piezo Speaker
  U1 = SWITCH_SPDT [package=kps-1290]
  LED1 = smd LED [color="Red (633nm)" package="0603 [SMD]"]
  R1 = Resistor [tolerance=±5% resistance=220 package="2512 [SMD]"]

nets:
  N1: Mod1.pin_3, Mod1.pin_8, Mod1.pin_13, Mod1.pin_18, Mod1.pin_23, Mod1.pin_28, Mod1.pin_33, Mod1.pin_38, OLED_I2C1.GND, S1.leg0, J1.pin1, U1.S, LED1.cathode
  N2: Mod1.pin_5, OLED_I2C1.VDD
  N3: Mod1.pin_20, J1.pin2
  N4: Mod1.pin_21, R1.Pin_1
  N5: Mod1.pin_29, OLED_I2C1.SCK
  N6: Mod1.pin_30, OLED_I2C1.SDA
  N7: Mod1.pin_39, U1.P
  N8: Mod1.pin_40, S1.leg1

custom parts:
  Raspberry Pi Pico W: Raspberry Pi Pico W. Based around the RP2040 microcontroller the Pico W is a low cost microcontroller device bringing Raspberry Pi quality, cost, and easy of use to the microcontroller space. The areas marked KEEPOUT in pcb silkscreen should not have traces running through them to avoid shorts on a soldered in module!
